// Logisim project new_CPU.circ as structural Verilog: 5 circuits, main circuit main
module main (
  output [3:0] out_1,
  output [3:0] out_2,
  output [3:0] out_3,
  output [3:0] out_4,
  output [3:0] out_5,
  output [3:0] out_6
);

  wire Adress, ALU, ALUCarry, ALULogic, and_1_out, and_2_out, clock_1_out, demultiplexer_1_out1, Digit,
       DoJump, FlagWrite, Jump, not_1_out, not_2_out, not_3_out, or_1_out, w, Write;
  wire [1:0] myalu_1_aeqb, register_1_q;
  wire [3:0] ALUop, multiplexer_1_out, Operation, Outp, RAMDigit;

  and and_1 (and_1_out, Digit, Adress);
  Demultiplexer #(.disabled("Z")) demultiplexer_1 (.out0(w), .out1(demultiplexer_1_out1), .in(Write), .sel(and_1_out));
  Multiplexer #(.disabled("Z"), .width(4)) multiplexer_1 (
    .in0(out_3), .in1(out_4), .out(multiplexer_1_out), .sel(not_1_out));
  not not_1 (not_1_out, Digit);
  RAM #(.addrWidth(4), .dataWidth(4)) ram_1 (
    .addr(multiplexer_1_out), .we(demultiplexer_1_out1), .oe(1'b1), .clk(demultiplexer_1_out1), .din(out_1),
    .dout(RAMDigit));
  MyALU myalu_1 (
    .Cin(ALUCarry), .Operation(ALUop), .A(out_3), .B(out_4), .M(ALULogic), .Outp(Outp),
    .AeqB(myalu_1_aeqb[0]), .Sign(myalu_1_aeqb[1]));
  Register #(.width(2)) register_1 (.D(myalu_1_aeqb), .clk(and_2_out), .Q(register_1_q));  // open: en, clr
  and and_2 (and_2_out, FlagWrite, not_2_out);
  not not_2 (not_2_out, clock_1_out);
  Clock clock_1 (.out(clock_1_out));
  OperationDecoder operationdecoder_1 (
    .Operation(Operation), .Digit(Digit), .Jump(Jump), .ALULogic(ALULogic), .ALU(ALU), .ALUCarry(ALUCarry),
    .FlagWrite(FlagWrite), .Adress(Adress), .ALUop(ALUop));
  nor nor_1 (Write, clock_1_out, Jump);
  or or_1 (or_1_out, register_1_q[1], register_1_q[0]);
  not not_3 (not_3_out, register_1_q[0]);
  Multiplexer #(.disabled("Z"), .select(2)) multiplexer_2 (
    .in0(register_1_q[0]), .in1(register_1_q[1]), .in2(or_1_out), .in3(not_3_out), .out(DoJump),
    .sel(ALUop[1:0]));
  PC pc_1 (.Clock(clock_1_out), .Operation(Operation), .A(out_5), .B(out_6));  // open: ClockWait, CA

  // Other names for the same wires on the sheet: A[3:0] = out_3; A_in[3:0] = out_5; B[3:0] = out_4; B_in[3:0] = out_6;
  //   Data[3:0] = out_1; ID[3:0] = out_2
endmodule

module MyALU (
  input  Cin,
  input  [3:0] Operation,
  input  [3:0] A,
  input  [3:0] B,
  input  M,
  output [3:0] Outp,
  output AeqB,
  output Sign
);

  wire n74181_1_p13, n74181_1_p14, n74181_1_p16, n74181_1_p18, not_2_out;

  // _74181 74181_1: pin names not known; wires that end beside it: B[0], A[1], A[0], B[1], Operation[3], A[2], Operation[2], B[2], Operation[1], A[3], Operation[0], B[3], n74181_1_p13, n74181_1_p14, M, n74181_1_p16, Outp[0], n74181_1_p18, Outp[1], AeqB, Outp[2], Outp[3]
  and and_1 (Sign, n74181_1_p14, not_2_out);
  not not_1 (n74181_1_p13, Cin);
  not not_2 (not_2_out, AeqB);

  // Notes on the sheet:
  //   Cout
  //   Pn
endmodule

module Registers (
  output [3:0] out_1,
  output [3:0] A,
  output [3:0] out_3,
  output [3:0] out_4,
  output [3:0] out_5,
  output [3:0] out_6,
  output [3:0] out_7,
  output [3:0] out_8,
  output [3:0] out_9,
  output [3:0] B
);

  wire r0_w, r1_w, r2_w, r3_w, r4_w, r5_w, r6_w, r7_w, w;
  wire [2:0] A_t, B_t, t;
  wire [3:0] Data;

  Register #(.width(4)) r0 (.D(Data), .clk(r0_w));  // open: en, Q, clr
  Register #(.width(4)) r1 (.D(Data), .clk(r1_w));  // open: en, Q, clr
  Register #(.width(4)) r2 (.D(Data), .clk(r2_w));  // open: en, Q, clr
  Register #(.width(4)) r3 (.D(Data), .clk(r3_w));  // open: en, Q, clr
  Register #(.width(4)) r4 (.D(Data), .clk(r4_w));  // open: en, Q, clr
  Register #(.width(4)) r5 (.D(Data), .clk(r5_w));  // open: en, Q, clr
  Register #(.width(4)) r6 (.D(Data), .clk(r6_w));  // open: en, Q, clr
  Register #(.width(4)) r7 (.D(Data), .clk(r7_w));  // open: en, Q, clr
  Demultiplexer #(.select(3)) demultiplexer_1 (
    .out0(r0_w), .out1(r1_w), .out2(r2_w), .out3(r3_w), .out4(r4_w), .out5(r5_w), .out6(r6_w), .out7(r7_w),
    .in(w), .sel(t));
  Multiplexer #(.select(3), .width(4)) multiplexer_1 (
    .in0(out_1), .in1(out_3), .in2(out_4), .in3(out_5), .in4(out_6), .in5(out_7), .in6(out_8), .in7(out_9),
    .out(A), .sel(A_t));
  Multiplexer #(.select(3), .width(4)) multiplexer_2 (
    .in0(out_1), .in1(out_3), .in2(out_4), .in3(out_5), .in4(out_6), .in5(out_7), .in6(out_8), .in7(out_9),
    .out(B), .sel(B_t));

  // Other names for the same wires on the sheet: r0[3:0] = out_1; r1[3:0] = out_3; r2[3:0] = out_4; r3[3:0] = out_5;
  //   r4[3:0] = out_6; r5[3:0] = out_7; r6[3:0] = out_8; r7[3:0] = out_9
endmodule

module PC (
  input  Clock,
  input  ClockWait,
  output [7:0] CA,
  output [3:0] Operation,
  output [3:0] A,
  output [3:0] B
);

  wire ClockUpd, not_1_out;
  wire [7:0] controlled_buffer_1_out, counter_1_q;

  Counter #(.ongoal("stay")) counter_1 (.clk(ClockUpd), .D(CA), .Q(counter_1_q));  // open: clr, load, up, count, carry
  assign controlled_buffer_1_out = not_1_out ? counter_1_q : 8'bz;  // Controlled_Buffer controlled_buffer_1
  ROM #(.dataWidth(12)) rom_1 (.addr(controlled_buffer_1_out), .data({B, A, Operation}));
  not not_1 (not_1_out, ClockWait);
  and and_1 (ClockUpd, not_1_out, Clock);

  // Other names for the same wires on the sheet: CurrAdress[7:0] = CA

  // Notes on the sheet:
  //   contents of rom_1 (hex, n*v repeats v):
  //   0 151 144 a45
endmodule

module OperationDecoder (
  input  [3:0] Operation,
  output Digit,
  output Jump,
  output ALULogic,
  output ALU,
  output ALUCarry,
  output FlagWrite,
  output Adress,
  output [3:0] ALUop
);

  wire [15:7] rom_1_data;

  ROM #(.addrWidth(4), .dataWidth(16)) rom_1 (
    .addr(Operation), .data({rom_1_data, Adress, FlagWrite, ALUCarry, ALU, ALULogic, Jump, Digit}));

  assign ALUop = Operation;

  // Notes on the sheet:
  //   contents of rom_1 (hex, n*v repeats v):
  //   0 1 41 40 c 0 38 0 0 8 0 0 4*2
endmodule
