// Logisim project main.circ as structural Verilog: 12 circuits, main circuit main
module main (
);

  wire button_1_out, clock_1_out, clock_2_out, cpu_1_mr, cpu_1_mw, cpu_1_nothalt, dipswitch_1_sw1,
       dipswitch_1_sw2;
  wire [7:0] cpu_1_dataout, ram_1_dout;
  wire [15:0] cpu_1_address;

  Clock #(.highDuration(2), .lowDuration(2)) clock_1 (.out(clock_1_out));
  DipSwitch #(.number(2)) dipswitch_1 (.sw1(dipswitch_1_sw1), .sw2(dipswitch_1_sw2));
  Button button_1 (.out(button_1_out));
  Clock clock_2 (.out(clock_2_out));
  CPU cpu_1 (
    .DataIn(ram_1_dout), .Clk(clock_1_out), .NotReset(dipswitch_1_sw1), .NotWait(dipswitch_1_sw2),
    .Irq(button_1_out), .DataOut(cpu_1_dataout), .NotHalt(cpu_1_nothalt), .MR(cpu_1_mr), .MW(cpu_1_mw),
    .Address(cpu_1_address));  // open: IntAck
  LED led_1 (.in(cpu_1_nothalt));
  RAM #(.addrWidth(16)) ram_1 (
    .addr(cpu_1_address), .we(cpu_1_mw), .oe(cpu_1_mr), .clk(clock_2_out), .din(cpu_1_dataout),
    .dout(ram_1_dout));
endmodule

module StackPointer (
  input  HFromD,
  input  NotReset,
  input  [7:0] DIn,
  input  LFromD,
  input  HToD,
  input  ToA,
  input  NotDec,
  input  NotInc,
  input  Clk,
  input  LToD,
  output [15:0] AOut,
  output [7:0] DOut
);

  wire n74193_1_pin4, n74193_1_pin5, n74193_1_pin11, n74193_2_pin4, n74193_2_pin5, n74193_3_pin4,
       n74193_3_pin5, n74193_3_pin11, n74193_4_pin4, n74193_4_pin5, not_1_out;
  wire [3:0] n74193_1_pin3, n74193_2_pin3;
  wire [7:0] n74193_4_pin3;

  not not_1 (not_1_out, NotReset);
  _74193 u_74193_1 (
    .pin1(DIn[5]), .pin2(n74193_1_pin3[1]), .pin3(n74193_1_pin3[0]), .pin4(n74193_1_pin4),
    .pin5(n74193_1_pin5), .pin6(n74193_1_pin3[2]), .pin7(n74193_1_pin3[3]), .pin15(DIn[4]),
    .pin14(not_1_out), .pin11(n74193_1_pin11), .pin10(DIn[6]), .pin9(DIn[7]));  // open: pin13, pin12
  assign DOut = HToD ? {n74193_1_pin3, n74193_2_pin3} : 8'bz;  // Controlled_Buffer controlled_buffer_1
  _74193 u_74193_2 (
    .pin1(DIn[1]), .pin2(n74193_2_pin3[1]), .pin3(n74193_2_pin3[0]), .pin4(n74193_2_pin4),
    .pin5(n74193_2_pin5), .pin6(n74193_2_pin3[2]), .pin7(n74193_2_pin3[3]), .pin15(DIn[0]),
    .pin14(not_1_out), .pin13(n74193_1_pin4), .pin12(n74193_1_pin5), .pin11(n74193_1_pin11), .pin10(DIn[2]),
    .pin9(DIn[3]));
  assign AOut = ToA ? {n74193_1_pin3, n74193_2_pin3, n74193_4_pin3} : 16'bz;  // Controlled_Buffer controlled_buffer_2
  _74193 u_74193_3 (
    .pin1(DIn[5]), .pin2(n74193_4_pin3[5]), .pin3(n74193_4_pin3[4]), .pin4(n74193_3_pin4),
    .pin5(n74193_3_pin5), .pin6(n74193_4_pin3[6]), .pin7(n74193_4_pin3[7]), .pin15(DIn[4]),
    .pin14(not_1_out), .pin13(n74193_2_pin4), .pin12(n74193_2_pin5), .pin11(n74193_3_pin11), .pin10(DIn[6]),
    .pin9(DIn[7]));
  Hex_Digit_Display hex_digit_display_1 (.value(n74193_1_pin3));  // open: dp
  _74193 u_74193_4 (
    .pin1(DIn[1]), .pin2(n74193_4_pin3[1]), .pin3(n74193_4_pin3[0]), .pin4(n74193_4_pin4),
    .pin5(n74193_4_pin5), .pin6(n74193_4_pin3[2]), .pin7(n74193_4_pin3[3]), .pin15(DIn[0]),
    .pin14(not_1_out), .pin13(n74193_3_pin4), .pin12(n74193_3_pin5), .pin11(n74193_3_pin11), .pin10(DIn[2]),
    .pin9(DIn[3]));
  assign DOut = LToD ? n74193_4_pin3 : 8'bz;  // Controlled_Buffer controlled_buffer_3
  Hex_Digit_Display hex_digit_display_2 (.value(n74193_2_pin3));  // open: dp
  Hex_Digit_Display hex_digit_display_3 (.value(n74193_4_pin3[7:4]));  // open: dp
  Hex_Digit_Display hex_digit_display_4 (.value(n74193_4_pin3[3:0]));  // open: dp
  not not_2 (n74193_1_pin11, HFromD);
  not not_3 (n74193_3_pin11, LFromD);
  or or_1 (n74193_4_pin4, NotDec, Clk);
  or or_2 (n74193_4_pin5, NotInc, Clk);
endmodule

module CPU (
  input  [7:0] DataIn,
  input  Clk,
  input  NotReset,
  input  NotWait,
  input  Irq,
  output [7:0] DataOut,
  output IntAck,
  output NotHalt,
  output MR,
  output MW,
  output [15:0] Address
);

  wire AccFromD, AccShLeft, AccShRight, AccToD, ALUCarry, ALUEnable, ALUMode, CnstToD, FRFromD, FRToD,
       FRUpdate, IRFromD, NotPCInc, NotSPDec, NotSPInc, or_1_out, PCHFromD, PCHToD, PCLFromD, PCLToD, PCToA,
       SCClear, SPHFromD, SPHToD, SPLFromD, SPLToD, SPToA, TmpHFromD, TmpHToD, TmpLFromD, TmpLToD, TmpToA;
  wire [2:0] alu_1_flagsout, Flags;
  wire [3:0] ALUSel, FromD, Step, ToD;
  wire [7:0] Accum, DBus, Instruction, temporaryregister_1_hout;
  wire [15:0] ABus;

  LedBar #(.matrixcols(3)) ledbar_1 (.led0(Flags[0]), .led1(Flags[1]), .led2(Flags[2]));
  Hex_Digit_Display hex_digit_display_1 (.value(Step));  // open: dp
  Hex_Digit_Display hex_digit_display_2 (.value(Accum[7:4]));  // open: dp
  Hex_Digit_Display hex_digit_display_3 (.value(Accum[3:0]));  // open: dp
  Hex_Digit_Display hex_digit_display_4 (.value(Instruction[7:4]));  // open: dp
  StackPointer stackpointer_1 (
    .HFromD(SPHFromD), .NotReset(NotReset), .DIn(DBus), .LFromD(SPLFromD), .HToD(SPHToD), .ToA(SPToA),
    .NotDec(NotSPDec), .NotInc(NotSPInc), .Clk(Clk), .LToD(SPLToD), .AOut(ABus), .DOut(DBus));
  Hex_Digit_Display hex_digit_display_5 (.value(Instruction[3:0]));  // open: dp
  Hex_Digit_Display hex_digit_display_6 (.value(DBus[7:4]));  // open: dp
  Hex_Digit_Display hex_digit_display_7 (.value(DBus[3:0]));  // open: dp
  RegisterFile registerfile_1 (.DIn(DBus), .FromD(FromD), .ToD(ToD), .NotReset(NotReset), .Clk(Clk), .DOut(DBus));
  Hex_Digit_Display hex_digit_display_8 (.value(ABus[15:12]));  // open: dp
  Hex_Digit_Display hex_digit_display_9 (.value(ABus[11:8]));  // open: dp
  Hex_Digit_Display hex_digit_display_10 (.value(ABus[7:4]));  // open: dp
  ProgramCounter programcounter_1 (
    .NotReset(NotReset), .HFromD(PCHFromD), .Clk(Clk), .HToD(PCHToD), .DIn(DBus), .ToA(PCToA),
    .LFromD(PCLFromD), .NotInc(NotPCInc), .LToD(PCLToD), .DOut(DBus), .AOut(ABus));
  Hex_Digit_Display hex_digit_display_11 (.value(ABus[3:0]));  // open: dp
  InstructionRegister instructionregister_1 (
    .DIn(DBus), .FromD(IRFromD), .Clk(Clk), .NotReset(NotReset), .Instruction(Instruction));
  Accumulator accumulator_1 (
    .ToD(AccToD), .DIn(DBus), .FromD(AccFromD), .ShiftLeft(AccShLeft), .ShiftRight(AccShRight), .Clk(Clk),
    .NotReset(NotReset), .DOut(DBus), .ALUOut(Accum));
  TemporaryRegister temporaryregister_1 (
    .ToA(TmpToA), .HToD(TmpHToD), .LToD(TmpLToD), .NotReset(NotReset), .HFromD(TmpHFromD), .Clk(Clk),
    .DIn(DBus), .LFromD(TmpLFromD), .AOut(ABus), .DOut(DBus), .HOut(temporaryregister_1_hout));
  assign DBus = CnstToD ? 8'h1c : 8'bz;  // Controlled_Buffer controlled_buffer_1
  ALU alu_1 (
    .DIn(Accum), .Enable(ALUEnable), .AccIn(temporaryregister_1_hout), .Sel(ALUSel), .Carry(ALUCarry),
    .Mode(ALUMode), .DOut(DBus), .FlagsOut(alu_1_flagsout));
  assign Address = or_1_out ? ABus : 16'bz;  // Controlled_Buffer controlled_buffer_2
  or or_1 (or_1_out, MR, MW);
  assign DBus = MR ? DataIn : 8'bz;  // Controlled_Buffer controlled_buffer_3
  assign DataOut = MW ? DBus : 8'bz;  // Controlled_Buffer controlled_buffer_4
  FlagRegister flagregister_1 (
    .FlagsIn(alu_1_flagsout), .DIn(DBus), .FromD(FRFromD), .Update(FRUpdate), .ToD(FRToD), .Clk(Clk),
    .NotReset(NotReset), .FlagsOut(Flags), .DOut(DBus));
  StepCounter stepcounter_1 (
    .Clk(Clk), .NotReset(NotReset), .Clear(SCClear), .NotHalt(NotHalt), .NotWait(NotWait), .Step(Step));
  InstructionDecoder instructiondecoder_1 (
    .Clk(Clk), .IntReq(Irq), .Instruction(Instruction), .Flags(Flags), .Step(Step), .MemFromD(MW),
    .SPHFromD(SPHFromD), .SPLFromD(SPLFromD), .PCHFromD(PCHFromD), .PCLFromD(PCLFromD),
    .TmpHFromD(TmpHFromD), .TmpLFromD(TmpLFromD), .AccFromD(AccFromD), .FromD(FromD), .FRFromD(FRFromD),
    .IRFromD(IRFromD), .ToD(ToD), .MemToD(MR), .SPHToD(SPHToD), .SPLToD(SPLToD), .PCHToD(PCHToD),
    .PCLToD(PCLToD), .TmpHToD(TmpHToD), .TmpLToD(TmpLToD), .AccToD(AccToD), .FRToD(FRToD), .CnstToD(CnstToD),
    .ALUMode(ALUMode), .ALUCarry(ALUCarry), .ALUSel(ALUSel), .SPToA(SPToA), .PCToA(PCToA), .TmpToA(TmpToA),
    .ALUEnable(ALUEnable), .FRUpdate(FRUpdate), .SCClear(SCClear), .NotPCInc(NotPCInc), .NotSPInc(NotSPInc),
    .NotSPDec(NotSPDec), .NotHalt(NotHalt), .IntAck(IntAck), .AccShLeft(AccShLeft), .AccShRight(AccShRight));

  // Other names for the same wires on the sheet: IntReq = Irq; MemFromD = MW; MemToD = MR
endmodule

module TemporaryRegister (
  input  ToA,
  input  HToD,
  input  LToD,
  input  NotReset,
  input  HFromD,
  input  Clk,
  input  [7:0] DIn,
  input  LFromD,
  output [15:0] AOut,
  output [7:0] DOut,
  output [7:0] HOut
);

  wire n74273_1_pin11, n74273_2_pin11;
  wire [7:0] n74273_2_pin2;

  _74273 u_74273_1 (
    .pin1(NotReset), .pin2(HOut[0]), .pin3(DIn[0]), .pin4(DIn[1]), .pin5(HOut[1]), .pin6(HOut[2]),
    .pin7(DIn[2]), .pin8(DIn[3]), .pin9(HOut[3]), .pin19(HOut[7]), .pin18(DIn[7]), .pin17(DIn[6]),
    .pin16(HOut[6]), .pin15(HOut[5]), .pin14(DIn[5]), .pin13(DIn[4]), .pin12(HOut[4]), .pin11(n74273_1_pin11));
  and and_1 (n74273_1_pin11, HFromD, Clk);
  assign AOut = ToA ? {HOut, n74273_2_pin2} : 16'bz;  // Controlled_Buffer controlled_buffer_1
  _74273 u_74273_2 (
    .pin1(NotReset), .pin2(n74273_2_pin2[0]), .pin3(DIn[0]), .pin4(DIn[1]), .pin5(n74273_2_pin2[1]),
    .pin6(n74273_2_pin2[2]), .pin7(DIn[2]), .pin8(DIn[3]), .pin9(n74273_2_pin2[3]), .pin19(n74273_2_pin2[7]),
    .pin18(DIn[7]), .pin17(DIn[6]), .pin16(n74273_2_pin2[6]), .pin15(n74273_2_pin2[5]), .pin14(DIn[5]),
    .pin13(DIn[4]), .pin12(n74273_2_pin2[4]), .pin11(n74273_2_pin11));
  assign DOut = HToD ? HOut : 8'bz;  // Controlled_Buffer controlled_buffer_2
  and and_2 (n74273_2_pin11, LFromD, Clk);
  assign DOut = LToD ? n74273_2_pin2 : 8'bz;  // Controlled_Buffer controlled_buffer_3
endmodule

module Accumulator (
  input  ToD,
  input  [7:0] DIn,
  input  FromD,
  input  ShiftLeft,
  input  ShiftRight,
  input  Clk,
  input  NotReset,
  output [7:0] DOut,
  output [7:0] ALUOut
);

  wire nand_1_out, not_1_out;
  wire [7:0] register_1_q;

  assign DOut = ToD ? register_1_q : 8'bz;  // Controlled_Buffer controlled_buffer_1
  Register register_1 (.D(DIn), .en(FromD), .clk(Clk), .Q(register_1_q), .clr(not_1_out));
  not not_1 (not_1_out, NotReset);
  assign ALUOut = ShiftRight ? {1'b0, register_1_q[7:1]} : 8'bz;  // Controlled_Buffer controlled_buffer_2
  assign ALUOut = ShiftLeft ? {register_1_q[6:0], 1'b0} : 8'bz;  // Controlled_Buffer controlled_buffer_3
  assign ALUOut = nand_1_out ? register_1_q : 8'bz;  // Controlled_Buffer controlled_buffer_4
  nand nand_1 (nand_1_out, ShiftLeft, ShiftRight);
endmodule

module ALU (
  input  [7:0] DIn,
  input  Enable,
  input  [7:0] AccIn,
  input  [3:0] Sel,
  input  Carry,
  input  Mode,
  output [7:0] DOut,
  output [2:0] FlagsOut
);

  wire n74181_1_p13, NotCarry, Sign, Zero;
  wire [6:0] n74181_2_p17;

  // _74181 74181_1: pin names not known; wires that end beside it: AccIn[4], DIn[5], DIn[4], AccIn[5], Sel[3], DIn[6], Sel[2], AccIn[6], Sel[1], DIn[7], Sel[0], AccIn[7], n74181_1_p13, Mode, NotCarry, n74181_2_p17[4], n74181_2_p17[5], Sign
  // _74181 74181_2: pin names not known; wires that end beside it: n74181_2_p17[6], AccIn[0], DIn[1], DIn[0], AccIn[1], Sel[3], DIn[2], Sel[2], AccIn[2], Sel[1], DIn[3], Sel[0], AccIn[3], Carry, Mode, n74181_1_p13, n74181_2_p17[0], n74181_2_p17[1], n74181_2_p17[2], n74181_2_p17[3]
  nor nor_1 (Zero, Sign, n74181_2_p17[6], n74181_2_p17[5], n74181_2_p17[4], n74181_2_p17[2], n74181_2_p17[0], n74181_2_p17[1], n74181_2_p17[3]);
  assign DOut = Enable ? {Sign, n74181_2_p17} : 8'bz;  // Controlled_Buffer controlled_buffer_1
  assign FlagsOut = Enable ? {Zero, NotCarry, Sign} : 3'bz;  // Controlled_Buffer controlled_buffer_2
endmodule

module FlagRegister (
  input  [2:0] FlagsIn,
  input  [7:0] DIn,
  input  FromD,
  input  Update,
  input  ToD,
  input  Clk,
  input  NotReset,
  output [2:0] FlagsOut,
  output [7:0] DOut
);

  wire not_1_out, or_1_out;
  wire [4:0] controlled_buffer_1_out, register_1_q;

  assign {controlled_buffer_1_out, FlagsIn} = FromD ? DIn : 8'bz;  // Controlled_Buffer controlled_buffer_1
  or or_1 (or_1_out, FromD, Update);
  Register register_1 (
    .D({controlled_buffer_1_out, FlagsIn}), .en(or_1_out), .clk(Clk), .Q({register_1_q, FlagsOut}),
    .clr(not_1_out));
  not not_1 (not_1_out, NotReset);
  assign DOut = ToD ? {register_1_q, FlagsOut} : 8'bz;  // Controlled_Buffer controlled_buffer_2
endmodule

module InstructionRegister (
  input  [7:0] DIn,
  input  FromD,
  input  Clk,
  input  NotReset,
  output [7:0] Instruction
);

  wire not_1_out;

  Register register_1 (.D(DIn), .en(FromD), .clk(Clk), .Q(Instruction), .clr(not_1_out));
  not not_1 (not_1_out, NotReset);
endmodule

module RegisterFile (
  input  [7:0] DIn,
  input  [3:0] FromD,
  input  [3:0] ToD,
  input  NotReset,
  input  Clk,
  output [7:0] DOut
);

  wire decoder_1_out9, decoder_1_out10, decoder_1_out11, decoder_1_out12, decoder_1_out13, decoder_1_out14,
       not_1_out;
  wire [7:0] demultiplexer_1_out9, demultiplexer_1_out10, demultiplexer_1_out11, demultiplexer_1_out12,
       demultiplexer_1_out13, register_1_q, register_2_q, register_3_q, register_4_q, register_5_q;

  Demultiplexer #(.enable("true"), .select(4), .width(8)) demultiplexer_1 (
    .out9(demultiplexer_1_out9), .out10(demultiplexer_1_out10), .out11(demultiplexer_1_out11),
    .out12(demultiplexer_1_out12), .out13(demultiplexer_1_out13), .in(DIn), .sel(FromD));  // open: out0, out1, out2, out3, out4, out5, out6, out7, out8, out14, out15, en
  Decoder #(.select(4)) decoder_1 (
    .out9(decoder_1_out9), .out10(decoder_1_out10), .out11(decoder_1_out11), .out12(decoder_1_out12),
    .out13(decoder_1_out13), .out14(decoder_1_out14), .sel(FromD));  // open: out0, out1, out2, out3, out4, out5, out6, out7, out8, out15, en
  not not_1 (not_1_out, NotReset);
  Register register_1 (.D(demultiplexer_1_out9), .en(decoder_1_out9), .clk(Clk), .Q(register_1_q), .clr(not_1_out));
  Register register_2 (.D(demultiplexer_1_out10), .en(decoder_1_out10), .clk(Clk), .Q(register_2_q), .clr(not_1_out));
  Register register_3 (.D(demultiplexer_1_out11), .en(decoder_1_out11), .clk(Clk), .Q(register_3_q), .clr(not_1_out));
  Register register_4 (.D(demultiplexer_1_out12), .en(decoder_1_out12), .clk(Clk), .Q(register_4_q), .clr(not_1_out));
  Register register_5 (.D(demultiplexer_1_out13), .en(decoder_1_out13), .clk(Clk), .Q(register_5_q), .clr(not_1_out));
  Multiplexer #(.enable("true"), .select(4), .width(8)) multiplexer_1 (
    .in9(register_1_q), .in10(register_2_q), .in11(register_3_q), .in12(register_4_q), .in13(register_5_q),
    .out(DOut), .sel(ToD));  // open: in0, in1, in2, in3, in4, in5, in6, in7, in8, in14, in15, en
endmodule

module InstructionDecoder (
  input  Clk,
  input  IntReq,
  input  [7:0] Instruction,
  input  [2:0] Flags,
  input  [3:0] Step,
  output MemFromD,
  output SPHFromD,
  output SPLFromD,
  output PCHFromD,
  output PCLFromD,
  output TmpHFromD,
  output TmpLFromD,
  output AccFromD,
  output [3:0] FromD,
  output FRFromD,
  output IRFromD,
  output [3:0] ToD,
  output MemToD,
  output SPHToD,
  output SPLToD,
  output PCHToD,
  output PCLToD,
  output TmpHToD,
  output TmpLToD,
  output AccToD,
  output FRToD,
  output CnstToD,
  output ALUMode,
  output ALUCarry,
  output [3:0] ALUSel,
  output SPToA,
  output PCToA,
  output TmpToA,
  output ALUEnable,
  output FRUpdate,
  output SCClear,
  output NotPCInc,
  output NotSPInc,
  output NotSPDec,
  output NotHalt,
  output IntAck,
  output AccShLeft,
  output AccShRight
);

  wire IntDisable, IntEnable, j_k_ff_1_q, j_k_ff_1_qn;
  wire [1:0] ToABus;
  wire [7:4] rom_4_data;
  wire [15:15] and_1_out;

  and and_1 (and_1_out[15], IntReq, j_k_ff_1_qn);
  J_K_Flip_Flop j_k_ff_1 (
    .J(IntDisable), .K(IntEnable), .clk(Clk), .Q(j_k_ff_1_q), .Qn(j_k_ff_1_qn));  // open: preset, reset
  ROM #(.addrWidth(16)) rom_1 (.addr({and_1_out[15], Step, Flags, Instruction}), .data({ToD, FromD}));
  ROM #(.addrWidth(16)) rom_2 (
    .addr({and_1_out[15], Step, Flags, Instruction}), .data({ALUSel, ALUCarry, ALUMode, ToABus}));
  ROM #(.addrWidth(16)) rom_3 (
    .addr({and_1_out[15], Step, Flags, Instruction}),
    .data({IntAck, NotHalt, NotSPDec, NotSPInc, NotPCInc, SCClear, FRUpdate, ALUEnable}));
  ROM #(.addrWidth(16)) rom_4 (
    .addr({and_1_out[15], Step, Flags, Instruction}),
    .data({rom_4_data, IntDisable, IntEnable, AccShRight, AccShLeft}));
  Decoder #(.select(4)) decoder_1 (
    .out1(MemFromD), .out2(SPHFromD), .out3(SPLFromD), .out4(PCHFromD), .out5(PCLFromD), .out6(TmpHFromD),
    .out7(TmpLFromD), .out8(AccFromD), .out14(FRFromD), .out15(IRFromD), .sel(FromD));  // open: out0, out9, out10, out11, out12, out13, en
  Decoder #(.select(2)) decoder_2 (.out1(SPToA), .out2(PCToA), .out3(TmpToA), .sel(ToABus));  // open: out0, en
  Decoder #(.select(4)) decoder_3 (
    .out1(MemToD), .out2(SPHToD), .out3(SPLToD), .out4(PCHToD), .out5(PCLToD), .out6(TmpHToD),
    .out7(TmpLToD), .out8(AccToD), .out14(FRToD), .out15(CnstToD), .sel(ToD));  // open: out0, out9, out10, out11, out12, out13, en

  // Other names for the same wires on the sheet: FromDBus[3:0] = FromD; ToDBus[3:0] = ToD

  // Notes on the sheet:
  //   contents of rom_1 (hex, n*v repeats v):
  //   1f 0 0 18 19 1a 1b 1c 1d 1e 12 19 1b 1d 7*16 5*d6 16 16 51 5*16 5*d6 89 8a 8b 8c 8d 8e 98 9a 9b 9c
  //   9d 9e a8 a9 ab ac ad ae b8 b9 ba bc bd be c8 c9 ca cb cd ce d8 d9 da db dc de e8 e9 ea eb ec ed d2
  //   2d 4d 81 91 a1 b1 c1 d1 e1 51 81 a1 c1 18 19 1a 1b 1c 1d 1e 19 1b 1d 17 d4 4*1f 17 d4 17 d4 1f 1f 17
  //   d4 16 1f 1f 16 16 1f 16 14 1f 1f 14 14 1f 14 86 96 a6 b6 c6 d6 86 96 a6 b6 c6 d6 86 96 a6 b6 c6 d6
  //   86 96 a6 b6 c6 d6 16 86 96 a6 b6 c6 d6 16 86 96 a6 b6 c6 d6 16 86 96 a6 b6 c6 d6 16 86 96 a6 b6 c6
  //   d6 16 86 96 a6 b6 c6 d6 16 86 96 a6 b6 c6 d6 16 86 96 a6 b6 c6 d6 16 49*0 1f 0 0 18 19 1a 1b 1c 1d
  //   1e 12 19 1b 1d 7*16 5*d6 16 16 51 5*16 5*d6 89 8a 8b 8c 8d 8e 98 9a 9b 9c 9d 9e a8 a9 ab ac ad ae b8
  //   b9 ba bc bd be c8 c9 ca cb cd ce d8 d9 da db dc de e8 e9 ea eb ec ed d2 2d 4d 81 91 a1 b1 c1 d1 e1
  //   51 81 a1 c1 18 19 1a 1b 1c 1d 1e 19 1b 1d 17 d4 4*1f 17 d4 1f 1f 17 d4 17 d4 16 1f 1f 16 1f 16 16 14
  //   1f 1f 14 1f 14 14 86 96 a6 b6 c6 d6 86 96 a6 b6 c6 d6 86 96 a6 b6 c6 d6 86 96 a6 b6 c6 d6 16 86 96
  //   a6 b6 c6 d6 16 86 96 a6 b6 c6 d6 16 86 96 a6 b6 c6 d6 16 86 96 a6 b6 c6 d6 16 86 96 a6 b6 c6 d6 16
  //   86 96 a6 b6 c6 d6 16 86 96 a6 b6 c6 d6 16 49*0 1f 0 0 18 19 1a 1b 1c 1d 1e 12 19 1b 1d 7*16 5*d6 16
  //   16 51 5*16 5*d6 89 8a 8b 8c 8d 8e 98 9a 9b 9c 9d 9e a8 a9 ab ac ad ae b8 b9 ba bc bd be c8 c9 ca cb
  //   cd ce d8 d9 da db dc de e8 e9 ea eb ec ed d2 2d 4d 81 91 a1 b1 c1 d1 e1 51 81 a1 c1 18 19 1a 1b 1c
  //   1d 1e 19 1b 1d 17 d4 1f 1f 17 d4 1f 1f 17 d4 1f 1f 17 d4 16 1f 16 1f 16 1f 16 14 1f 14 1f 14 1f 14
  //   86 96 a6 b6 c6 d6 86 96 a6 b6 c6 d6 86 96 a6 b6 c6 d6 86 96 a6 b6 c6 d6 16 86 96 a6 b6 c6 d6 16 86
  //   96 a6 b6 c6 d6 16 86 96 a6 b6 c6 d6 16 86 96 a6 b6 c6 d6 16 86 96 a6 b6 c6 d6 16 86 96 a6 b6 c6 d6
  //   16 86 96 a6 b6 c6 d6 16 49*0 1f 0 0 18 19 1a 1b 1c 1d 1e 12 19 1b 1d 7*16 5*d6 16 16 51 5*16 5*d6 89
  //   8a 8b 8c 8d 8e 98 9a 9b 9c 9d 9e a8 a9 ab ac ad ae b8 b9 ba bc bd be c8 c9 ca cb cd ce d8 d9 da db
  //   dc de e8 e9 ea eb ec ed d2 2d 4d 81 91 a1 b1 c1 d1 e1 51 81 a1 c1 18 19 1a 1b 1c 1d 1e 19 1b 1d 17
  //   d4 1f 1f 17 d4 4*1f 17 d4 17 d4 16 1f 16 1f 1f 16 16 14 1f 14 1f 1f 14 14 86 96 a6 b6 c6 d6 86 96 a6
  //   b6 c6 d6 86 96 a6 b6 c6 d6 86 96 a6 b6 c6 d6 16 86 96 a6 b6 c6 d6 16 86 96 a6 b6 c6 d6 16 86 96 a6
  //   b6 c6 d6 16 86 96 a6 b6 c6 d6 16 86 96 a6 b6 c6 d6 16 86 96 a6 b6 c6 d6 16 86 96 a6 b6 c6 d6 16 49*0
  //   1f 0 0 18 19 1a 1b 1c 1d 1e 12 19 1b 1d 7*16 5*d6 16 16 51 5*16 5*d6 89 8a 8b 8c 8d 8e 98 9a 9b 9c
  //   9d 9e a8 a9 ab ac ad ae b8 b9 ba bc bd be c8 c9 ca cb cd ce d8 d9 da db dc de e8 e9 ea eb ec ed d2
  //   2d 4d 81 91 a1 b1 c1 d1 e1 51 81 a1 c1 18 19 1a 1b 1c 1d 1e 19 1b 1d 1f 1f 17 d4 1f 1f 17 d4 17 d4
  //   1f 1f 17 d4 1f 16 1f 16 16 1f 16 1f 14 1f 14 14 1f 14 86 96 a6 b6 c6 d6 86 96 a6 b6 c6 d6 86 96 a6
  //   b6 c6 d6 86 96 a6 b6 c6 d6 16 86 96 a6 b6 c6 d6 16 86 96 a6 b6 c6 d6 16 86 96 a6 b6 c6 d6 16 86 96
  //   a6 b6 c6 d6 16 86 96 a6 b6 c6 d6 16 86 96 a6 b6 c6 d6 16 86 96 a6 b6 c6 d6 16 49*0 1f 0 0 18 19 1a
  //   1b 1c 1d 1e 12 19 1b 1d 7*16 5*d6 16 16 51 5*16 5*d6 89 8a 8b 8c 8d 8e 98 9a 9b 9c 9d 9e a8 a9 ab ac
  //   ad ae b8 b9 ba bc bd be c8 c9 ca cb cd ce d8 d9 da db dc de e8 e9 ea eb ec ed d2 2d 4d 81 91 a1 b1
  //   c1 d1 e1 51 81 a1 c1 18 19 1a 1b 1c 1d 1e 19 1b 1d 1f 1f 17 d4 1f 1f 17 d4 1f 1f 17 d4 17 d4 1f 16
  //   1f 16 1f 16 16 1f 14 1f 14 1f 14 14 86 96 a6 b6 c6 d6 86 96 a6 b6 c6 d6 86 96 a6 b6 c6 d6 86 96 a6
  //   b6 c6 d6 16 86 96 a6 b6 c6 d6 16 86 96 a6 b6 c6 d6 16 86 96 a6 b6 c6 d6 16 86 96 a6 b6 c6 d6 16 86
  //   96 a6 b6 c6 d6 16 86 96 a6 b6 c6 d6 16 86 96 a6 b6 c6 d6 16 49*0 1f 0 0 18 19 1a 1b 1c 1d 1e 12 19
  //   1b 1d 7*16 5*d6 16 16 51 5*16 5*d6 89 8a 8b 8c 8d 8e 98 9a 9b 9c 9d 9e a8 a9 ab ac ad ae b8 b9 ba bc
  //   bd be c8 c9 ca cb cd ce d8 d9 da db dc de e8 e9 ea eb ec ed d2 2d 4d 81 91 a1 b1 c1 d1 e1 51 81 a1
  //   c1 18 19 1a 1b 1c 1d 1e 19 1b 1d 1f 1f 17 d4 17 d4 1f 1f 17 d4 1f 1f 17 d4 1f 16 16 1f 16 1f 16 1f
  //   14 14 1f 14 1f 14 86 96 a6 b6 c6 d6 86 96 a6 b6 c6 d6 86 96 a6 b6 c6 d6 86 96 a6 b6 c6 d6 16 86 96
  //   a6 b6 c6 d6 16 86 96 a6 b6 c6 d6 16 86 96 a6 b6 c6 d6 16 86 96 a6 b6 c6 d6 16 86 96 a6 b6 c6 d6 16
  //   86 96 a6 b6 c6 d6 16 8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
  //   contents of rom_2 (hex, n*v repeats v):
  //   a 8 8 18*a 5*8 a a 9 5*a 50*8 21*9 a 8 5*a 8 a 8 a a a 8 7*a 9 a a 9 9 a 9 74*8 49*0 a 8 8 18*a 5*8
  //   a a 9 5*a 50*8 21*9 a 8 5*a 8 a a a 8 a 8 7*a 9 a a 9 a 9 9 74*8 49*0 a 8 8 18*a 5*8 a a 9 5*a 50*8
  //   21*9 a 8 a a a 8 a a a 8 a a a 8 7*a 9 a 9 a 9 a 9 74*8 49*0 a 8 8 18*a 5*8 a a 9 5*a 50*8 21*9 a 8
  //   a a a 8 5*a 8 a 8 7*a 9 a 9 a a 9 9 74*8 49*0 a 8 8 18*a 5*8 a a 9 5*a 50*8 21*9 a a a 8 a a a 8 a 8
  //   a a a 8 8*a 9 a 9 9 a 9 74*8 49*0 a 8 8 18*a 5*8 a a 9 5*a 50*8 21*9 a a a 8 a a a 8 a a a 8 a 8 8*a
  //   9 a 9 a 9 9 74*8 49*0 a 8 8 18*a 5*8 a a 9 5*a 50*8 21*9 a a a 8 a 8 a a a 8 a a a 8 8*a 9 9 a 9 a 9
  //   74*8 49*0 a 8 8 18*a 5*8 a a 9 5*a 50*8 21*9 a a a 8 a 8 5*a 8 a 8 8*a 9 9 a a 9 9 74*8 50*0 20*a
  //   5*8 a a 9 5*a 5*8 42*a 8 8 8 7*a 4*9 7*a 9 9 9 a 8 4*0 a 8 a 8 0 0 a 8 a 0 0 a a 0 a 9 0 0 9 9 0 9
  //   6*0 6*f8 6*c 7*98 7*68 7*4c 7*c 7*6c 7*1c 7*90 7*f0 50*0 20*a 5*8 a a 9 5*a 5*8 42*a 8 8 8 7*a 4*9
  //   7*a 9 9 9 a 8 4*0 a 8 0 0 a 8 a 8 a 0 0 a 0 a a 9 0 0 9 0 9 9 6*0 6*f8 6*c 7*98 7*68 7*4c 7*c 7*6c
  //   7*1c 7*90 7*f0 50*0 20*a 5*8 a a 9 5*a 5*8 42*a 8 8 8 7*a 4*9 7*a 9 9 9 a 8 0 0 a 8 0 0 a 8 0 0 a 8
  //   a 0 a 0 a 0 a 9 0 9 0 9 0 9 6*0 6*f8 6*c 7*98 7*68 7*4c 7*c 7*6c 7*1c 7*98 7*f8 50*0 20*a 5*8 a a 9
  //   5*a 5*8 42*a 8 8 8 7*a 4*9 7*a 9 9 9 a 8 0 0 a 8 4*0 a 8 a 8 a 0 a 0 0 a a 9 0 9 0 0 9 9 6*0 6*f8
  //   6*c 7*98 7*68 7*4c 7*c 7*6c 7*1c 7*98 7*f8 50*0 20*a 5*8 a a 9 5*a 5*8 42*a 8 8 8 7*a 4*9 7*a 9 9 9
  //   0 0 a 8 0 0 a 8 a 8 0 0 a 8 0 a 0 a a 0 a 0 9 0 9 9 0 9 6*0 6*f8 6*c 7*98 7*68 7*4c 7*c 7*6c 7*1c
  //   7*90 7*f0 50*0 20*a 5*8 a a 9 5*a 5*8 42*a 8 8 8 7*a 4*9 7*a 9 9 9 0 0 a 8 0 0 a 8 0 0 a 8 a 8 0 a 0
  //   a 0 a a 0 9 0 9 0 9 9 6*0 6*f8 6*c 7*98 7*68 7*4c 7*c 7*6c 7*1c 7*90 7*f0 50*0 20*a 5*8 a a 9 5*a
  //   5*8 42*a 8 8 8 7*a 4*9 7*a 9 9 9 0 0 a 8 a 8 0 0 a 8 0 0 a 8 0 a a 0 a 0 a 0 9 9 0 9 0 9 6*0 6*f8
  //   6*c 7*98 7*68 7*4c 7*c 7*6c 7*1c 7*98 7*f8 50*0 20*a 5*8 a a 9 5*a 5*8 42*a 8 8 8 7*a 4*9 7*a 9 9 9
  //   0 0 a 8 a 8 4*0 a 8 a 8 0 a a 0 0 a a 0 9 9 0 0 9 9 6*0 6*f8 6*c 7*98 7*68 7*4c 7*c 7*6c 7*1c 7*98
  //   7*f8 59*0 4*a 14*b 8 10*b 42*0 a a a 7*0 4*a 7*0 a a a 8 a 4*0 8 a 8 a 0 0 8 a 9 0 0 9 9 0 9 a 0 0 a
  //   a 0 75*a 59*0 4*a 14*b 8 10*b 42*0 a a a 7*0 4*a 7*0 a a a 8 a 4*0 8 a 0 0 8 a 8 a 9 0 0 9 0 9 9 a 0
  //   0 a 0 76*a 59*0 4*a 14*b 8 10*b 42*0 a a a 7*0 4*a 7*0 a a a 8 a 0 0 8 a 0 0 8 a 0 0 8 a 9 0 9 0 9 0
  //   9 a 0 a 0 a 0 75*a 59*0 4*a 14*b 8 10*b 42*0 a a a 7*0 4*a 7*0 a a a 8 a 0 0 8 a 4*0 8 a 8 a 9 0 9 0
  //   0 9 9 a 0 a 0 0 76*a 59*0 4*a 14*b 8 10*b 42*0 a a a 7*0 4*a 7*0 a a a 0 0 8 a 0 0 8 a 8 a 0 0 8 a 0
  //   9 0 9 9 0 9 0 a 0 a a 0 75*a 59*0 4*a 14*b 8 10*b 42*0 a a a 7*0 4*a 7*0 a a a 0 0 8 a 0 0 8 a 0 0 8
  //   a 8 a 0 9 0 9 0 9 9 0 a 0 a 0 76*a 59*0 4*a 14*b 8 10*b 42*0 a a a 7*0 4*a 7*0 a a a 0 0 8 a 8 a 0 0
  //   8 a 0 0 8 a 0 9 9 0 9 0 9 0 a a 0 a 0 75*a 59*0 4*a 14*b 8 10*b 42*0 a a a 7*0 4*a 7*0 a a a 0 0 8 a
  //   8 a 4*0 8 a 8 a 0 9 9 0 0 9 9 0 a a 0 0 76*a 63*0 14*a 8 10*a 66*0 a 5*0 a 0 a 0 0 0 a 0 9 0 0 9 9 0
  //   9 144*0 14*a 8 10*a 66*0 a 5*0 a 0 0 0 a 0 a 0 9 0 0 9 0 9 9 144*0 14*a 8 10*a 66*0 a 0 0 0 a 0 0 0
  //   a 0 0 0 a 0 9 0 9 0 9 0 9 144*0 14*a 8 10*a 66*0 a 0 0 0 a 5*0 a 0 a 0 9 0 9 0 0 9 9 144*0 14*a 8
  //   10*a 68*0 a 0 0 0 a 0 a 0 0 0 a 0 0 9 0 9 9 0 9 144*0 14*a 8 10*a 68*0 a 0 0 0 a 0 0 0 a 0 a 0 0 9 0
  //   9 0 9 9 144*0 14*a 8 10*a 68*0 a 0 a 0 0 0 a 0 0 0 a 0 0 9 9 0 9 0 9 144*0 14*a 8 10*a 68*0 a 0 a
  //   5*0 a 0 a 0 0 9 9 0 0 9 9 158*0 a 90*0 8 0 0 8 8 0 8 158*0 a 90*0 8 0 0 8 0 8 8 158*0 a 90*0 8 0 8 0
  //   8 0 8 158*0 a 90*0 8 0 8 0 0 8 8 158*0 a 91*0 8 0 8 8 0 8 158*0 a 91*0 8 0 8 0 8 8 158*0 a 91*0 8 8
  //   0 8 0 8 158*0 a 91*0 8 8 0 0 8 8 249*0 8 0 0 8 8 0 8 249*0 8 0 0 8 0 8 8 249*0 8 0 8 0 8 0 8 249*0 8
  //   0 8 0 0 8 8 250*0 8 0 8 8 0 8 250*0 8 0 8 0 8 8 250*0 8 8 0 8 0 8 250*0 8 8 0 0 8 8 249*0 a 0 0 a a
  //   0 a 249*0 a 0 0 a 0 a a 249*0 a 0 a 0 a 0 a 249*0 a 0 a 0 0 a a 250*0 a 0 a a 0 a 250*0 a 0 a 0 a a
  //   250*0 a a 0 a 0 a 250*0 a a 0 0 a a 18562*0 8 8 8 18*a 5*8 a a 9 5*a 50*8 21*9 a 5*8 a 8 a 8 8 8 a 8
  //   a 8 8 a a 8 a 9 8 8 9 9 8 9 74*8 49*0 8 8 8 18*a 5*8 a a 9 5*a 50*8 21*9 a 5*8 a 8 8 8 a 8 a 8 a 8 8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
  //   contents of rom_3 (hex, n*v repeats v):
  //   74 78 78 18*70 5*78 70 70 58 5*70 50*78 11*58 10*68 70 78 4*74 70 78 70 78 74 74 70 78 70 74 74 70
  //   70 74 70 68 74 74 68 68 74 68 74*78 49*0 74 78 78 18*70 5*78 70 70 58 5*70 50*78 11*58 10*68 70 78
  //   4*74 70 78 74 74 70 78 70 78 70 74 74 70 74 70 70 68 74 74 68 74 68 68 74*78 49*0 74 78 78 18*70
  //   5*78 70 70 58 5*70 50*78 11*58 10*68 70 78 74 74 70 78 74 74 70 78 74 74 70 78 70 74 70 74 70 74 70
  //   68 74 68 74 68 74 68 74*78 49*0 74 78 78 18*70 5*78 70 70 58 5*70 50*78 11*58 10*68 70 78 74 74 70
  //   78 4*74 70 78 70 78 70 74 70 74 74 70 70 68 74 68 74 74 68 68 74*78 49*0 74 78 78 18*70 5*78 70 70
  //   58 5*70 50*78 11*58 10*68 74 74 70 78 74 74 70 78 70 78 74 74 70 78 74 70 74 70 70 74 70 74 68 74 68
  //   68 74 68 74*78 49*0 74 78 78 18*70 5*78 70 70 58 5*70 50*78 11*58 10*68 74 74 70 78 74 74 70 78 74
  //   74 70 78 70 78 74 70 74 70 74 70 70 74 68 74 68 74 68 68 74*78 49*0 74 78 78 18*70 5*78 70 70 58
  //   5*70 50*78 11*58 10*68 74 74 70 78 70 78 74 74 70 78 74 74 70 78 74 70 70 74 70 74 70 74 68 68 74 68
  //   74 68 74*78 49*0 74 78 78 18*70 5*78 70 70 58 5*70 50*78 11*58 10*68 74 74 70 78 70 78 4*74 70 78 70
  //   78 74 70 70 74 74 70 70 74 68 68 74 74 68 68 74*78 50*0 9*74 11*70 5*78 70 70 58 5*70 5*78 42*74 78
  //   78 78 7*74 4*58 7*74 68 68 68 78 78 4*0 4*78 0 0 78 78 70 0 0 70 70 0 70 68 0 0 68 68 0 68 74*7b
  //   50*0 9*74 11*70 5*78 70 70 58 5*70 5*78 42*74 78 78 78 7*74 4*58 7*74 68 68 68 78 78 4*0 78 78 0 0
  //   4*78 70 0 0 70 0 70 70 68 0 0 68 0 68 68 74*7b 50*0 9*74 11*70 5*78 70 70 58 5*70 5*78 42*74 78 78
  //   78 7*74 4*58 7*74 68 68 68 78 78 0 0 78 78 0 0 78 78 0 0 78 78 70 0 70 0 70 0 70 68 0 68 0 68 0 68
  //   74*7b 50*0 9*74 11*70 5*78 70 70 58 5*70 5*78 42*74 78 78 78 7*74 4*58 7*74 68 68 68 78 78 0 0 78 78
  //   4*0 4*78 70 0 70 0 0 70 70 68 0 68 0 0 68 68 74*7b 50*0 9*74 11*70 5*78 70 70 58 5*70 5*78 42*74 78
  //   78 78 7*74 4*58 7*74 68 68 68 0 0 78 78 0 0 4*78 0 0 78 78 0 70 0 70 70 0 70 0 68 0 68 68 0 68 74*7b
  //   50*0 9*74 11*70 5*78 70 70 58 5*70 5*78 42*74 78 78 78 7*74 4*58 7*74 68 68 68 0 0 78 78 0 0 78 78 0
  //   0 4*78 0 70 0 70 0 70 70 0 68 0 68 0 68 68 74*7b 50*0 9*74 11*70 5*78 70 70 58 5*70 5*78 42*74 78 78
  //   78 7*74 4*58 7*74 68 68 68 0 0 4*78 0 0 78 78 0 0 78 78 0 70 70 0 70 0 70 0 68 68 0 68 0 68 74*7b
  //   50*0 9*74 11*70 5*78 70 70 58 5*70 5*78 42*74 78 78 78 7*74 4*58 7*74 68 68 68 0 0 4*78 4*0 4*78 0
  //   70 70 0 0 70 70 0 68 68 0 0 68 68 74*7b 59*0 4*74 14*78 f8 10*78 42*0 74 74 74 7*0 4*74 7*0 74 74 74
  //   78 74 4*0 78 74 78 74 0 0 78 74 58 0 0 58 58 0 58 74 0 0 74 74 0 75*74 59*0 4*74 14*78 f8 10*78 42*0
  //   74 74 74 7*0 4*74 7*0 74 74 74 78 74 4*0 78 74 0 0 78 74 78 74 58 0 0 58 0 58 58 74 0 0 74 0 76*74
  //   59*0 4*74 14*78 f8 10*78 42*0 74 74 74 7*0 4*74 7*0 74 74 74 78 74 0 0 78 74 0 0 78 74 0 0 78 74 58
  //   0 58 0 58 0 58 74 0 74 0 74 0 75*74 59*0 4*74 14*78 f8 10*78 42*0 74 74 74 7*0 4*74 7*0 74 74 74 78
  //   74 0 0 78 74 4*0 78 74 78 74 58 0 58 0 0 58 58 74 0 74 0 0 76*74 59*0 4*74 14*78 f8 10*78 42*0 74 74
  //   74 7*0 4*74 7*0 74 74 74 0 0 78 74 0 0 78 74 78 74 0 0 78 74 0 58 0 58 58 0 58 0 74 0 74 74 0 75*74
  //   59*0 4*74 14*78 f8 10*78 42*0 74 74 74 7*0 4*74 7*0 74 74 74 0 0 78 74 0 0 78 74 0 0 78 74 78 74 0
  //   58 0 58 0 58 58 0 74 0 74 0 76*74 59*0 4*74 14*78 f8 10*78 42*0 74 74 74 7*0 4*74 7*0 74 74 74 0 0
  //   78 74 78 74 0 0 78 74 0 0 78 74 0 58 58 0 58 0 58 0 74 74 0 74 0 75*74 59*0 4*74 14*78 f8 10*78 42*0
  //   74 74 74 7*0 4*74 7*0 74 74 74 0 0 78 74 78 74 4*0 78 74 78 74 0 58 58 0 0 58 58 0 74 74 0 0 76*74
  //   63*0 14*74 78 10*74 66*0 74 5*0 74 0 74 0 0 0 74 0 58 0 0 58 58 0 58 144*0 14*74 78 10*74 66*0 74
  //   5*0 74 0 0 0 74 0 74 0 58 0 0 58 0 58 58 144*0 14*74 78 10*74 66*0 74 0 0 0 74 0 0 0 74 0 0 0 74 0
  //   58 0 58 0 58 0 58 144*0 14*74 78 10*74 66*0 74 0 0 0 74 5*0 74 0 74 0 58 0 58 0 0 58 58 144*0 14*74
  //   78 10*74 68*0 74 0 0 0 74 0 74 0 0 0 74 0 0 58 0 58 58 0 58 144*0 14*74 78 10*74 68*0 74 0 0 0 74 0
  //   0 0 74 0 74 0 0 58 0 58 0 58 58 144*0 14*74 78 10*74 68*0 74 0 74 0 0 0 74 0 0 0 74 0 0 58 58 0 58 0
  //   58 144*0 14*74 78 10*74 68*0 74 0 74 5*0 74 0 74 0 0 58 58 0 0 58 58 158*0 74 90*0 78 0 0 78 78 0 78
  //   158*0 74 90*0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
  //   contents of rom_4 (hex, n*v repeats v):
  //   0 4 8 254*0 4 8 254*0 4 8 254*0 4 8 254*0 4 8 254*0 4 8 254*0 4 8 254*0 4 8 30974*0 4 8 254*0 4 8
  //   254*0 4 8 254*0 4 8 254*0 4 8 254*0 4 8 254*0 4 8 254*0 4 8
endmodule

module StepCounter (
  input  Clk,
  input  NotReset,
  input  Clear,
  input  NotHalt,
  input  NotWait,
  output [3:0] Step
);

  wire and_1_out, n74161_1_pin3, n74161_1_pin4, n74161_1_pin5, n74161_1_pin6, n74161_1_pin10, not_1_out;

  not not_1 (not_1_out, Clear);
  and and_1 (and_1_out, NotHalt, NotWait);
  _74161 u_74161_1 (
    .pin1(NotReset), .pin2(Clk), .pin3(n74161_1_pin3), .pin4(n74161_1_pin4), .pin5(n74161_1_pin5),
    .pin6(n74161_1_pin6), .pin7(and_1_out), .pin14(Step[0]), .pin13(Step[1]), .pin12(Step[2]),
    .pin11(Step[3]), .pin10(n74161_1_pin10), .pin9(not_1_out));  // open: pin15
  // also tied to GND on the sheet: {n74161_1_pin3, n74161_1_pin4, n74161_1_pin5, n74161_1_pin6}
  // also tied to VCC on the sheet: n74161_1_pin10
endmodule

module ProgramCounter (
  input  NotReset,
  input  HFromD,
  input  Clk,
  input  HToD,
  input  [7:0] DIn,
  input  ToA,
  input  LFromD,
  input  NotInc,
  input  LToD,
  output [7:0] DOut,
  output [15:0] AOut
);

  wire counter_2_carry, not_1_out, not_2_out;
  wire [3:0] counter_1_q, counter_1_q_2, counter_2_q, counter_2_q_2;

  not not_1 (not_1_out, NotReset);
  not not_2 (not_2_out, NotInc);
  Counter counter_1 (
    .clr(not_1_out), .load(HFromD), .up(counter_2_carry), .count(counter_2_carry), .clk(Clk), .D(DIn),
    .Q({counter_1_q_2, counter_1_q}));  // open: carry
  Counter counter_2 (
    .clr(not_1_out), .load(LFromD), .up(not_2_out), .count(not_2_out), .clk(Clk), .D(DIn),
    .carry(counter_2_carry), .Q({counter_2_q_2, counter_2_q}));
  assign DOut = HToD ? {counter_1_q_2, counter_1_q} : 8'bz;  // Controlled_Buffer controlled_buffer_1
  assign AOut = ToA ? {counter_1_q_2, counter_1_q, counter_2_q_2, counter_2_q} : 16'bz;  // Controlled_Buffer controlled_buffer_2
  assign DOut = LToD ? {counter_2_q_2, counter_2_q} : 8'bz;  // Controlled_Buffer controlled_buffer_3
  Hex_Digit_Display hex_digit_display_1 (.value(counter_1_q_2));  // open: dp
  Hex_Digit_Display hex_digit_display_2 (.value(counter_1_q));  // open: dp
  Hex_Digit_Display hex_digit_display_3 (.value(counter_2_q_2));  // open: dp
  Hex_Digit_Display hex_digit_display_4 (.value(counter_2_q));  // open: dp
endmodule
